# Fritzing sketch 8H+2Vites (saved by Fritzing 0.9.10b)
breadboards: 1

parts:
  S1 = Toggle Switch [package=THT]
  S2 = Toggle Switch [package=THT]
  S3 = Toggle Switch [package=THT]
  S4 = Toggle Switch [package=THT]
  S5 = Toggle Switch [package=THT]
  S6 = Toggle Switch [package=THT]
  S7 = Toggle Switch [package=THT]
  S8 = Toggle Switch [package=THT]
  S9 = Toggle Switch [package=THT]
  S10 = Toggle Switch [package=THT]
  Parça1 = Arduino Leonardo (Rev3b)

nets:
  N1: S1.L1, S2.L1, S3.L1, S4.L1, S5.L1, S6.L1, S7.L1, S8.L1, S9.L1, S10.L1
  N2: S1.COM, Parça1.D10_PWM/A10
  N3: S1.L2, S2.L2, S3.L2, S4.L2, S5.L2, S6.L2, S7.L2, S8.L2, S9.L2, S10.L2
  N4: S2.COM, Parça1.D6_PWM/A7
  N5: S3.COM, Parça1.D5_PWM
  N6: S4.COM, Parça1.D4/A6
  N7: S5.COM, Parça1.D3_PWM/SCL
  N8: S6.COM, Parça1.D7
  N9: S7.COM, Parça1.D8/A8
  N10: S8.COM, Parça1.D9_PWM/A9
  N11: S9.COM, Parça1.A4
  N12: S10.COM, Parça1.A5
