# Fritzing sketch Pedal Files (saved by Fritzing 0.9.10b)
breadboards: 1

parts:
  Parça1 = Arduino Nano (Rev3.0)
  U1 = POT [knob_status=50% power=0.5W package=alps_pot]
  U2 = POT [knob_status=50% power=0.5W package=alps_pot]
  U3 = POT [knob_status=50% power=0.5W package=alps_pot]

nets:
  N1: Parça1.GND, U1.A, U2.A, U3.A
  N2: Parça1.5V, U1.E, U2.E, U3.E
  N3: Parça1.A2, U1.S
  N4: Parça1.A1, U2.S
  N5: Parça1.A0, U3.S
